# Fritzing sketch LEDMatrixGuesser (saved by Fritzing 0.9.3b)
breadboards: 1

parts:
  Part1 = Arduino Uno (Rev3)
  LED1 = smd LED [color="Red (633nm)" package="0603 [SMD]"]
  R1 = Resistor [tolerance=±5% resistance=220 package="1206 [SMD]"]
  LED4 = smd LED [color="Red (633nm)" package="0603 [SMD]"]
  R2 = Resistor [tolerance=±5% resistance=220 package="1206 [SMD]"]
  LED5 = smd LED [color="Red (633nm)" package="0603 [SMD]"]
  R3 = Resistor [tolerance=±5% resistance=220 package="1206 [SMD]"]
  LED6 = smd LED [color="Red (633nm)" package="0603 [SMD]"]
  LED7 = smd LED [color="Red (633nm)" package="0603 [SMD]"]
  LED8 = smd LED [color="Red (633nm)" package="0603 [SMD]"]
  LED9 = smd LED [color="Red (633nm)" package="0603 [SMD]"]
  R4 = Resistor [tolerance=±5% resistance=220 package="1206 [SMD]"]
  LED10 = smd LED [color="Red (633nm)" package="0603 [SMD]"]
  LED11 = smd LED [color="Red (633nm)" package="0603 [SMD]"]
  R5 = Resistor [tolerance=±5% resistance=220 package="1206 [SMD]"]
  R6 = Resistor [tolerance=±5% resistance=220 package="1206 [SMD]"]
  R7 = Trimmer Potentiometer [maximum_resistance=10kΩ package=THT]
  R8 = Trimmer Potentiometer [maximum_resistance=10kΩ package=THT]
  S1 = Pushbutton [package="[SMD]"]
  R9 = Resistor [tolerance=±5% resistance=10k package="1206 [SMD]"]

nets:
  N1: Part1.A0, R7.wiper
  N2: Part1.A1, R8.wiper
  N3: Part1.D8, LED9.anode
  N4: Part1.D9_PWM, LED10.anode
  N5: Part1.D10_PWM/SS, LED11.anode
  N6: Part1.D11_PWM/MOSI, S1.Pin_1, S1.Pin_2, R9.Pin_1
  N7: Part1.D2, LED1.anode
  N8: Part1.D3_PWM, LED4.anode
  N9: Part1.D4, LED5.anode
  N10: Part1.D5_PWM, LED6.anode
  N11: Part1.D6_PWM, LED7.anode
  N12: Part1.D7, LED8.anode
  N13: Part1.5V, R7.leg2, R8.leg2, S1.Pin_3, S1.Pin_4
  N14: Part1.GND, R1.Pin_1, R2.Pin_1, R3.Pin_1, R4.Pin_1, R5.Pin_1, R6.Pin_1, R7.leg1, R8.leg1, R9.Pin_0
  N15: LED1.cathode, R1.Pin_0, LED6.cathode
  N16: LED4.cathode, R2.Pin_0, LED7.cathode
  N17: LED5.cathode, R3.Pin_0, LED8.cathode
  N18: LED9.cathode, R4.Pin_0
  N19: LED10.cathode, R5.Pin_0
  N20: LED11.cathode, R6.Pin_0
